// Logisim project lab3_part1_4bit_adder.circ as structural Verilog: 1 circuit, main circuit full_adder_4bit
module full_adder_4bit (
  input  Cin,
  input  [3:0] A,
  input  [3:0] B,
  output [3:0] S,
  output Cout
);

  Adder #(.width(4)) adder_1 (.a(A), .b(B), .out(S), .cin(Cin), .cout(Cout));
endmodule
