// Logisim project lab3_part2_2bit_addsub.circ as structural Verilog: 1 circuit, main circuit main
module main (
  input  Sub,
  input  [1:0] A,
  input  [1:0] B,
  output [1:0] S,
  output Cout
);

  wire adder_1_cout, not_1_out;
  wire [1:0] xor_1_out;

  assign xor_1_out = B ^ {2{Sub}};  // XOR_Gate xor_1, 2 bits wide
  Adder #(.width(2)) adder_1 (.a(A), .b(xor_1_out), .out(S), .cin(Sub), .cout(adder_1_cout));
  and and_1 (Cout, adder_1_cout, not_1_out);
  not not_1 (not_1_out, Sub);
endmodule
