// Logisim project lab3_part3_bcd_adder.circ as structural Verilog: 1 circuit, main circuit main
module main (
  input  Cin,
  input  [3:0] A,
  input  [3:0] B,
  output [3:0] S,
  output Digit2
);

  wire adder_1_cout, and_1_out, or_2_out;
  wire [3:0] adder_1_out, adder_2_out;

  or or_1 (Digit2, adder_1_cout, and_1_out);
  and and_1 (and_1_out, adder_1_out[3], or_2_out);
  or or_2 (or_2_out, adder_1_out[2], adder_1_out[1]);
  Adder #(.width(4)) adder_1 (.a(A), .b(B), .out(adder_1_out), .cin(Cin), .cout(adder_1_cout));
  Multiplexer #(.width(4)) multiplexer_1 (.in0(adder_1_out), .in1(adder_2_out), .out(S), .sel(Digit2));
  Adder #(.width(4)) adder_2 (.a(adder_1_out), .b(4'b0110), .out(adder_2_out));  // open: cin, cout
endmodule
